# Fritzing sketch Wiring (saved by Fritzing 0.9.3b)
breadboards: 1

parts:
  Part1 = Arduino Uno (Rev3) - ICSP
  FC-1 = Sound Sensor
  FC-2 = Sound Sensor
  FC-3 = Sound Sensor
  LED1 = LED - 5mm [color="Red (633nm)" package="5 mm [THT]"]
  LED2 = LED - 5mm [color="Red (633nm)" package="5 mm [THT]"]
  LED3 = LED - 5mm [color="Red (633nm)" package="5 mm [THT]"]
  R1 = Resistor [tolerance=±5% resistance=220 package=THT]
  R2 = Resistor [tolerance=±5% resistance=220 package=THT]  # not connected
  R3 = Resistor [tolerance=±5% resistance=220 package=THT]  # not connected
  Grove1 = Grove OLED 128x96

nets:
  N1: Part1.A0, FC-2.OUT
  N2: Part1.A1, FC-1.OUT
  N3: Part1.A2, FC-3.OUT
  N4: Part1.A4/SDA, Grove1.SDA
  N5: Part1.A5/SCL, Grove1.SCL
  VCC: Part1.5V, FC-1.VCC, FC-2.VCC, FC-3.VCC, Grove1.VCC
  GND: Part1.GND, FC-1.GND, FC-2.GND, FC-3.GND, LED1.cathode, LED2.cathode, LED3.cathode, Grove1.GND
  N6: LED1.anode, R1.Pin_0

notes:
  Microphone 1
  Microphone 2
  Microphone 3
  LCD DISPLAY
  1
  2
  3
